// Logisim project BKA.circ as structural Verilog: 1 circuit, main circuit main
module main (
  input  [7:0] A,
  input  [7:0] B,
  input  in_3,
  output out_4,
  output [7:0] out_5
);

  wire and_1_out, and_2_out, and_3_out, and_4_out, and_5_out, and_6_out, and_7_out, and_8_out, and_9_out,
       and_10_out, and_11_out, and_12_out, and_13_out, and_14_out, and_15_out, and_16_out, and_17_out,
       and_18_out, C_2_out, C_3_out, C_4_out, C_5_out, C_6_out, C_7_out, C_8_out, G_2_out, G_3_out, G_4_out,
       G_5_out, G_6_out, G_7_out, G_8_out, G_9_out, G_10_out, G_11_out, G_12_out, G_13_out, G_14_out,
       G_15_out, G_16_out, G_17_out, G_18_out, G_out, P_2_out, P_3_out, P_4_out, P_5_out, P_6_out, P_7_out,
       P_8_out, P_9_out, P_10_out, P_11_out, P_12_out, P_13_out, P_14_out, P_15_out, P_16_out, P_17_out,
       P_18_out, P_out;

  and and_1 (and_1_out, P_4_out, in_3);
  or C (out_4, G_4_out, and_1_out);
  xor S (out_5[7], P_out, C_2_out);
  xor P (P_out, A[7], B[7]);
  and G (G_out, A[7], B[7]);
  and and_2 (and_2_out, P_out, G_5_out);
  or G_2 (G_2_out, G_out, and_2_out);
  and and_3 (and_3_out, P_2_out, G_8_out);
  or G_3 (G_3_out, G_2_out, and_3_out);
  and and_4 (and_4_out, P_3_out, G_13_out);
  or G_4 (G_4_out, G_3_out, and_4_out);
  or C_2 (C_2_out, G_6_out, and_5_out);
  and P_2 (P_2_out, P_out, P_5_out);
  and P_3 (P_3_out, P_2_out, P_8_out);
  and P_4 (P_4_out, P_3_out, P_13_out);
  and and_5 (and_5_out, P_6_out, in_3);
  xor S_2 (out_5[6], P_5_out, C_3_out);
  xor P_5 (P_5_out, A[6], B[6]);
  and G_5 (G_5_out, A[6], B[6]);
  and and_6 (and_6_out, P_5_out, G_9_out);
  or G_6 (G_6_out, G_5_out, and_6_out);
  and and_7 (and_7_out, P_9_out, in_3);
  or C_3 (C_3_out, G_9_out, and_7_out);
  and P_6 (P_6_out, P_5_out, P_9_out);
  xor S_3 (out_5[5], P_7_out, C_4_out);
  and G_7 (G_7_out, A[5], B[5]);
  xor P_7 (P_7_out, A[5], B[5]);
  and and_8 (and_8_out, P_7_out, G_10_out);
  and P_8 (P_8_out, P_7_out, P_10_out);
  or G_8 (G_8_out, G_7_out, and_8_out);
  and and_9 (and_9_out, P_8_out, G_13_out);
  or G_9 (G_9_out, G_8_out, and_9_out);
  and and_10 (and_10_out, P_10_out, in_3);
  or C_4 (C_4_out, G_10_out, and_10_out);
  and P_9 (P_9_out, P_8_out, P_13_out);
  xor S_4 (out_5[4], P_10_out, C_5_out);
  and G_10 (G_10_out, A[4], B[4]);
  xor P_10 (P_10_out, A[4], B[4]);
  and and_11 (and_11_out, P_13_out, in_3);
  or C_5 (C_5_out, G_13_out, and_11_out);
  and G_11 (G_11_out, A[3], B[3]);
  or G_12 (G_12_out, G_11_out, and_12_out);
  xor S_5 (out_5[3], P_11_out, C_6_out);
  xor P_11 (P_11_out, A[3], B[3]);
  and P_12 (P_12_out, P_11_out, P_14_out);
  and and_12 (and_12_out, P_11_out, G_14_out);
  and and_13 (and_13_out, P_12_out, G_17_out);
  and P_13 (P_13_out, P_12_out, P_17_out);
  or G_13 (G_13_out, G_12_out, and_13_out);
  and and_14 (and_14_out, P_15_out, in_3);
  or C_6 (C_6_out, G_15_out, and_14_out);
  and G_14 (G_14_out, A[2], B[2]);
  or G_15 (G_15_out, G_14_out, and_15_out);
  xor S_6 (out_5[2], P_14_out, C_7_out);
  xor P_14 (P_14_out, A[2], B[2]);
  and P_15 (P_15_out, P_14_out, P_17_out);
  and and_15 (and_15_out, P_14_out, G_17_out);
  and and_16 (and_16_out, P_17_out, in_3);
  or C_7 (C_7_out, G_17_out, and_16_out);
  xor S_7 (out_5[1], P_16_out, C_8_out);
  and G_16 (G_16_out, A[1], B[1]);
  and and_17 (and_17_out, P_16_out, G_18_out);
  or G_17 (G_17_out, G_16_out, and_17_out);
  or C_8 (C_8_out, G_18_out, and_18_out);
  xor P_16 (P_16_out, A[1], B[1]);
  and P_17 (P_17_out, P_16_out, P_18_out);
  and and_18 (and_18_out, P_18_out, in_3);
  and G_18 (G_18_out, A[0], B[0]);
  xor S_8 (out_5[0], P_18_out, in_3);
  xor P_18 (P_18_out, A[0], B[0]);
endmodule
