// Logisim project KSA.circ as structural Verilog: 1 circuit, main circuit main
module main (
  input  [7:0] A,
  input  [7:0] B,
  input  Cin,
  output Cout,
  output [7:0] SUM
);

  wire and_1_out, and_2_out, and_3_out, and_4_out, and_5_out, and_6_out, and_7_out, and_8_out, and_9_out,
       and_10_out, and_11_out, and_12_out, and_13_out, and_14_out, and_15_out, and_16_out, and_17_out,
       and_18_out, and_19_out, and_20_out, and_21_out, and_22_out, and_23_out, and_24_out, and_25_out,
       and_26_out, and_27_out, and_28_out, and_29_out, and_30_out, and_31_out, and_32_out, and_33_out,
       and_34_out, and_35_out, and_36_out, and_37_out, and_38_out, and_39_out, and_40_out, and_41_out,
       and_42_out, G_2_out, G_3_out, G_4_out, G_5_out, G_6_out, G_7_out, G_8_out, G_out, or_2_out, or_3_out,
       or_4_out, or_5_out, or_6_out, or_7_out, or_8_out, or_9_out, or_10_out, or_11_out, or_12_out,
       or_13_out, or_14_out, or_15_out, or_16_out, or_17_out, or_18_out, or_19_out, or_20_out, or_21_out,
       or_22_out, or_23_out, or_24_out, or_25_out, P_2_out, P_3_out, P_4_out, P_5_out, P_6_out, P_7_out,
       P_8_out, P_out;

  and and_1 (and_1_out, and_7_out, Cin);
  or or_1 (Cout, or_4_out, and_1_out);
  and G (G_out, A[7], B[7]);
  xor P (P_out, A[7], B[7]);
  and and_2 (and_2_out, P_out, P_2_out);
  or or_2 (or_2_out, G_out, and_2_out);
  and and_3 (and_3_out, and_4_out, or_10_out);
  or or_3 (or_3_out, or_2_out, and_3_out);
  or or_4 (or_4_out, or_3_out, and_6_out);
  xor xor_1 (SUM[7], P_out, or_5_out);
  and and_4 (and_4_out, P_out, P_2_out);
  and and_5 (and_5_out, and_4_out, and_19_out);
  and and_6 (and_6_out, and_5_out, or_15_out);
  and and_7 (and_7_out, and_5_out, and_27_out);
  and and_8 (and_8_out, and_14_out, Cin);
  or or_5 (or_5_out, or_8_out, and_8_out);
  xor P_2 (P_2_out, A[6], B[6]);
  and G_2 (G_2_out, A[6], B[6]);
  and and_9 (and_9_out, P_2_out, G_3_out);
  or or_6 (or_6_out, G_2_out, and_9_out);
  and and_10 (and_10_out, and_11_out, or_14_out);
  or or_7 (or_7_out, or_6_out, and_10_out);
  or or_8 (or_8_out, or_7_out, and_13_out);
  xor xor_2 (SUM[6], P_2_out, or_9_out);
  and and_11 (and_11_out, P_2_out, P_3_out);
  and and_12 (and_12_out, and_11_out, and_26_out);
  and and_13 (and_13_out, and_12_out, or_19_out);
  and and_14 (and_14_out, and_12_out, and_34_out);
  and and_15 (and_15_out, and_21_out, Cin);
  or or_9 (or_9_out, or_12_out, and_15_out);
  xor xor_3 (SUM[5], P_3_out, or_13_out);
  xor P_3 (P_3_out, A[5], B[5]);
  and G_3 (G_3_out, A[5], B[5]);
  and and_16 (and_16_out, P_3_out, G_4_out);
  or or_10 (or_10_out, G_3_out, and_16_out);
  and and_17 (and_17_out, and_19_out, or_18_out);
  or or_11 (or_11_out, or_10_out, and_17_out);
  and and_18 (and_18_out, and_20_out, or_22_out);
  or or_12 (or_12_out, or_11_out, and_18_out);
  and and_19 (and_19_out, P_3_out, P_4_out);
  and and_20 (and_20_out, and_19_out, and_30_out);
  and and_21 (and_21_out, and_20_out, and_39_out);
  and and_22 (and_22_out, and_28_out, Cin);
  or or_13 (or_13_out, or_16_out, and_22_out);
  xor xor_4 (SUM[4], P_4_out, or_17_out);
  xor P_4 (P_4_out, A[4], B[4]);
  and G_4 (G_4_out, A[4], B[4]);
  and and_23 (and_23_out, P_4_out, G_5_out);
  or or_14 (or_14_out, G_4_out, and_23_out);
  and and_24 (and_24_out, and_26_out, or_21_out);
  or or_15 (or_15_out, or_14_out, and_24_out);
  and and_25 (and_25_out, and_27_out, G_8_out);
  or or_16 (or_16_out, or_15_out, and_25_out);
  and and_26 (and_26_out, P_4_out, P_5_out);
  and and_27 (and_27_out, and_26_out, and_35_out);
  and and_28 (and_28_out, and_27_out, P_8_out);
  and and_29 (and_29_out, and_34_out, Cin);
  or or_17 (or_17_out, or_19_out, and_29_out);
  and G_5 (G_5_out, A[3], B[3]);
  or or_18 (or_18_out, G_5_out, and_31_out);
  xor xor_5 (SUM[3], P_5_out, or_20_out);
  xor P_5 (P_5_out, A[3], B[3]);
  and and_30 (and_30_out, P_5_out, P_6_out);
  and and_31 (and_31_out, P_5_out, G_6_out);
  and and_32 (and_32_out, and_30_out, or_24_out);
  or or_19 (or_19_out, or_18_out, and_32_out);
  and and_33 (and_33_out, and_39_out, Cin);
  or or_20 (or_20_out, or_22_out, and_33_out);
  and and_34 (and_34_out, and_30_out, and_41_out);
  and G_6 (G_6_out, A[2], B[2]);
  or or_21 (or_21_out, G_6_out, and_36_out);
  xor xor_6 (SUM[2], P_6_out, or_23_out);
  xor P_6 (P_6_out, A[2], B[2]);
  and and_35 (and_35_out, P_6_out, P_7_out);
  and and_36 (and_36_out, P_6_out, G_7_out);
  and and_37 (and_37_out, and_35_out, G_8_out);
  or or_22 (or_22_out, or_21_out, and_37_out);
  and and_38 (and_38_out, and_41_out, Cin);
  or or_23 (or_23_out, or_24_out, and_38_out);
  and and_39 (and_39_out, and_35_out, P_8_out);
  and G_7 (G_7_out, A[1], B[1]);
  and and_40 (and_40_out, P_7_out, G_8_out);
  or or_24 (or_24_out, G_7_out, and_40_out);
  xor xor_7 (SUM[1], P_7_out, or_25_out);
  xor P_7 (P_7_out, A[1], B[1]);
  and and_41 (and_41_out, P_7_out, P_8_out);
  and and_42 (and_42_out, P_8_out, Cin);
  or or_25 (or_25_out, G_8_out, and_42_out);
  and G_8 (G_8_out, A[0], B[0]);
  xor xor_8 (SUM[0], P_8_out, Cin);
  xor P_8 (P_8_out, A[0], B[0]);
endmodule
